// Logisim project regfile.circ as structural Verilog: 1 circuit, main circuit regfile
module regfile (
  input  [4:0] ReadIndex1,
  input  [4:0] ReadIndex2,
  input  [4:0] WriteIndex,
  input  [31:0] WriteData,
  input  RegWEn,
  input  clk,
  output [31:0] ra,
  output [31:0] sp,
  output [31:0] t0,
  output [31:0] t1,
  output [31:0] t2,
  output [31:0] s0,
  output [31:0] s1,
  output [31:0] a0,
  output [31:0] ReadData1,
  output [31:0] ReadData2
);

  wire x1en;
  wire [31:0] x1;

  Decoder #(.select(5)) decoder_1 (
    .out1(x1en), .sel(WriteIndex), .en(RegWEn));  // open: out0, out2, out3, out4, out5, out6, out7, out8, out9, out10, out11, out12, out13, out14, out15, out16, out17, out18, out19, out20, out21, out22, out23, out24, out25, out26, out27, out28, out29, out30, out31
  Multiplexer #(.select(5), .width(32)) multiplexer_1 (
    .out(ReadData1), .sel(ReadIndex1));  // open: in0, in1, in2, in3, in4, in5, in6, in7, in8, in9, in10, in11, in12, in13, in14, in15, in16, in17, in18, in19, in20, in21, in22, in23, in24, in25, in26, in27, in28, in29, in30, in31
  Register #(.width(32)) register_1 (.D(WriteData), .en(x1en), .clk(clk), .Q(x1));  // open: clr
  Register #(.width(32)) register_2 (.D(WriteData), .en(x1en), .clk(clk), .Q(x1));  // open: clr
  Register #(.width(32)) register_3 (.D(WriteData), .en(x1en), .clk(clk), .Q(x1));  // open: clr
  Register #(.width(32)) register_4 (.D(WriteData), .en(x1en), .clk(clk), .Q(x1));  // open: clr
  Register #(.width(32)) register_5 (.D(WriteData), .en(x1en), .clk(clk), .Q(x1));  // open: clr
  Register #(.width(32)) register_6 (.D(WriteData), .en(x1en), .clk(clk), .Q(x1));  // open: clr
  Register #(.width(32)) register_7 (.D(WriteData), .en(x1en), .clk(clk), .Q(x1));  // open: clr
  Register #(.width(32)) register_8 (.D(WriteData), .en(x1en), .clk(clk), .Q(x1));  // open: clr
  Register #(.width(32)) register_9 (.D(WriteData), .en(x1en), .clk(clk), .Q(x1));  // open: clr
  Register #(.width(32)) register_10 (.D(WriteData), .en(x1en), .clk(clk), .Q(x1));  // open: clr
  Register #(.width(32)) register_11 (.D(WriteData), .en(x1en), .clk(clk), .Q(x1));  // open: clr
  Register #(.width(32)) register_12 (.D(WriteData), .en(x1en), .clk(clk), .Q(x1));  // open: clr
  Register #(.width(32)) register_13 (.D(WriteData), .en(x1en), .clk(clk), .Q(x1));  // open: clr
  Register #(.width(32)) register_14 (.D(WriteData), .en(x1en), .clk(clk), .Q(x1));  // open: clr
  Register #(.width(32)) register_15 (.D(WriteData), .en(x1en), .clk(clk), .Q(x1));  // open: clr
  Register #(.width(32)) register_16 (.D(WriteData), .en(x1en), .clk(clk), .Q(x1));  // open: clr
  Register #(.width(32)) register_17 (.D(WriteData), .en(x1en), .clk(clk), .Q(x1));  // open: clr
  Register #(.width(32)) register_18 (.D(WriteData), .en(x1en), .clk(clk), .Q(x1));  // open: clr
  Register #(.width(32)) register_19 (.D(WriteData), .en(x1en), .clk(clk), .Q(x1));  // open: clr
  Register #(.width(32)) register_20 (.D(WriteData), .en(x1en), .clk(clk), .Q(x1));  // open: clr
  Register #(.width(32)) register_21 (.D(WriteData), .en(x1en), .clk(clk), .Q(x1));  // open: clr
  Register #(.width(32)) register_22 (.D(WriteData), .en(x1en), .clk(clk), .Q(x1));  // open: clr
  Register #(.width(32)) register_23 (.D(WriteData), .en(x1en), .clk(clk), .Q(x1));  // open: clr
  Register #(.width(32)) register_24 (.D(WriteData), .en(x1en), .clk(clk), .Q(x1));  // open: clr
  Register #(.width(32)) register_25 (.D(WriteData), .en(x1en), .clk(clk), .Q(x1));  // open: clr
  Register #(.width(32)) register_26 (.D(WriteData), .en(x1en), .clk(clk), .Q(x1));  // open: clr
  Register #(.width(32)) register_27 (.D(WriteData), .en(x1en), .clk(clk), .Q(x1));  // open: clr
  Register #(.width(32)) register_28 (.D(WriteData), .en(x1en), .clk(clk), .Q(x1));  // open: clr
  Register #(.width(32)) register_29 (.D(WriteData), .en(x1en), .clk(clk), .Q(x1));  // open: clr
  Register #(.width(32)) register_30 (.D(WriteData), .en(x1en), .clk(clk), .Q(x1));  // open: clr
  Register #(.width(32)) register_31 (.D(WriteData), .en(x1en), .clk(clk), .Q(x1));  // open: clr
  Register #(.width(32)) register_32 (.D(WriteData), .en(x1en), .clk(clk), .Q(x1));  // open: clr

  // Notes on the sheet:
  //   INPUTS to your circuit
  //   DON'T CHANGE THE LOCATIONS OF THE INPUTS AND OUTPUTS!
  //   These are DEBUG/TEST outputs from your circuit.
  //   OUTPUTS from your circuit
endmodule
